# Fritzing sketch wiring_diagram_leonardo (saved by Fritzing 0.9.6b)
breadboards: 1

parts:
  Bauteil1 = Arduino Leonardo (Rev3b)
  range = Momentary Switch [package=ksa_sealed_tac_switch]
  splitter = Momentary Switch [package=ksa_sealed_tac_switch]
  comfort_shift = Momentary Switch [package=ksa_sealed_tac_switch]

nets:
  N1: Bauteil1.D0/RX, comfort_shift.1, comfort_shift.2
  N2: Bauteil1.D1/TX, splitter.1, splitter.2
  N3: Bauteil1.D2/SDA, Bauteil1.SDA, range.1, range.2
  N4: Bauteil1.GND, range.3, range.4, splitter.3, splitter.4, comfort_shift.3, comfort_shift.4
